# Fritzing sketch base circuit (saved by Fritzing 0.9.5d)
breadboards: 1

parts:
  Mod1 = Raspberry Pi Pico W
  LED1 = LED - 5mm [color="Red (633nm)" package="5 mm [THT]"]
  LED2 = LED - 5mm [color="Yellow (595nm)" package="5 mm [THT]"]
  LED3 = LED - 5mm [color="Green (565nm)" package="5 mm [THT]"]
  LED4 = LED - 5mm [color="Red (633nm)" package="5 mm [THT]"]
  LED5 = LED - 5mm [color="Yellow (595nm)" package="5 mm [THT]"]
  LED6 = LED - 5mm [color="Green (565nm)" package="5 mm [THT]"]
  LED7 = LED - 5mm [color="Red (633nm)" package="5 mm [THT]"]
  LED8 = LED - 5mm [color="Yellow (595nm)" package="5 mm [THT]"]
  LED9 = LED - 5mm [color="Green (565nm)" package="5 mm [THT]"]
  Part1 = TM1637

nets:
  N1: Mod1.pin_5, LED3.anode
  N2: Mod1.pin_6, LED2.anode
  N3: Mod1.pin_7, LED1.anode
  N4: Mod1.pin_9, LED7.anode
  N5: Mod1.pin_10, LED8.anode
  N6: Mod1.pin_11, LED9.anode
  N7: Mod1.pin_12, LED4.anode
  N8: Mod1.pin_14, LED6.anode
  N9: Mod1.pin_15, LED5.anode
  N10: Mod1.pin_21, Part1.CLK
  N11: Mod1.pin_22, Part1.DIO
  N12: Mod1.pin_33, Mod1.pin_38, Mod1.pin_42, LED1.cathode, LED2.cathode, LED3.cathode, LED4.cathode, LED5.cathode, LED6.cathode, LED7.cathode, LED8.cathode, LED9.cathode, Part1.VCC
  N13: Mod1.pin_36, Part1.GND

notes:
  Zone 1
  Zone 3
  Zone 2

custom parts:
  Raspberry Pi Pico W: Raspberry Pi Pico W. Based around the RP2040 microcontroller the Pico W is a low cost microcontroller device bringing Raspberry Pi quality, cost, and easy of use to the microcontroller space. The areas marked KEEPOUT in pcb silkscreen should not have traces running through them to avoid shorts on a soldered in module!
  TM1637: A 4 7-seg display
